# Fritzing sketch Schematische Tekening ESP32 -  I2C OLED (saved by Fritzing 0.9.3b)

parts:
  U1 = lolin
  OLED1 = OLED 128x64 I2C Monochrome Display

nets:
  N1: U1.connector14, OLED1.VDD
  N2: U1.connector15, OLED1.GND
  N3: U1.connector29, OLED1.SDA
  N4: U1.connector33, OLED1.SCK
