# Fritzing sketch Schematische Tekening Raspberry Pi Zero W - DHT22 (saved by Fritzing 0.9.3b)

parts:
  MCU1 = Raspberry Pi Zero
  LED1 = LEDs [package=led10mm]
  DHT1 = DHT22 Humidity and Temperature Sensor

nets:
  N1: MCU1.pin_2, MCU1.pin_4, DHT1.VDD
  N2: MCU1.pin_6, MCU1.pin_9, MCU1.pin_30, LED1.C, DHT1.GND
  N3: MCU1.pin_7, DHT1.DATA
  N4: MCU1.pin_8, LED1.A
